# Fritzing sketch DemoControlPanel (saved by Fritzing 0.9.5d)
breadboards: 1

parts:
  J1 = Generic shrouded header - 64 pins [form="♂ (shrouded male)" package=THT]
  LED1 = Red LED - 5mm [package="5 mm [THT]"]
  R1 = 220 Ω Resistor [package="0603 [SMD]"]
  S1 = Pushbutton [package="[THT]"]
  S2 = Pushbutton [package="[THT]"]
  S3 = Pushbutton [package="[THT]"]
  S4 = Pushbutton [package="[THT]"]
  S5 = Pushbutton [package="[THT]"]
  S6 = Pushbutton [package="[THT]"]
  S7 = Pushbutton [package="[THT]"]
  LED2 = Red LED - 5mm [package="5 mm [THT]"]
  LED3 = Red LED - 5mm [package="5 mm [THT]"]
  LED4 = Red LED - 5mm [package="5 mm [THT]"]
  R2 = 220 Ω Resistor [package="0603 [SMD]"]
  LED5 = Red LED - 5mm [package="5 mm [THT]"]
  LED6 = Red LED - 5mm [package="5 mm [THT]"]
  LED7 = Red LED - 5mm [package="5 mm [THT]"]
  R3 = 220 Ω Resistor [package="0603 [SMD]"]
  R4 = 220 Ω Resistor [package="0603 [SMD]"]
  R5 = 220 Ω Resistor [package="0603 [SMD]"]
  R6 = 220 Ω Resistor [package="0603 [SMD]"]
  R7 = 220 Ω Resistor [package="0603 [SMD]"]
  LED8 = Red LED - 5mm [package="5 mm [THT]"]
  LED9 = Red LED - 5mm [package="5 mm [THT]"]
  LED10 = Red LED - 5mm [package="5 mm [THT]"]
  LED11 = Red LED - 5mm [package="5 mm [THT]"]
  LED12 = Red LED - 5mm [package="5 mm [THT]"]
  LED13 = Red LED - 5mm [package="5 mm [THT]"]
  LED14 = Red LED - 5mm [package="5 mm [THT]"]
  LED15 = Red LED - 5mm [package="5 mm [THT]"]
  LED16 = Red LED - 5mm [package="5 mm [THT]"]
  LED17 = Red LED - 5mm [package="5 mm [THT]"]
  LED18 = Red LED - 5mm [package="5 mm [THT]"]
  LED19 = Red LED - 5mm [package="5 mm [THT]"]
  LED20 = Red LED - 5mm [package="5 mm [THT]"]
  R8 = 220 Ω Resistor [package="0603 [SMD]"]
  R9 = 220 Ω Resistor [package="0603 [SMD]"]
  R10 = 220 Ω Resistor [package="0603 [SMD]"]
  R11 = 220 Ω Resistor [package="0603 [SMD]"]
  R12 = 220 Ω Resistor [package="0603 [SMD]"]
  R13 = 220 Ω Resistor [package="0603 [SMD]"]
  R14 = 220 Ω Resistor [package="0603 [SMD]"]
  LED21 = Red LED - 5mm [package="5 mm [THT]"]
  R15 = 220 Ω Resistor [package="0603 [SMD]"]
  R16 = 220 Ω Resistor [package="0603 [SMD]"]
  R17 = 220 Ω Resistor [package="0603 [SMD]"]
  R18 = 220 Ω Resistor [package="0603 [SMD]"]
  R19 = 220 Ω Resistor [package="0603 [SMD]"]
  R20 = 220 Ω Resistor [package="0603 [SMD]"]
  R21 = 220 Ω Resistor [package="0603 [SMD]"]
  S8 = Pushbutton [package="[THT]"]
  S9 = Pushbutton [package="[THT]"]
  S10 = Pushbutton [package="[THT]"]
  S11 = Pushbutton [package="[THT]"]
  S12 = Pushbutton [package="[THT]"]
  S13 = Pushbutton [package="[THT]"]
  S14 = Pushbutton [package="[THT]"]
  S15 = Pushbutton [package="[THT]"]
  S16 = Pushbutton [package="[THT]"]
  S17 = Pushbutton [package="[THT]"]
  S18 = Pushbutton [package="[THT]"]
  S19 = Pushbutton [package="[THT]"]
  S20 = Pushbutton [package="[THT]"]
  S21 = Pushbutton [package="[THT]"]

nets:
  3.3V: J1.pin1, J1.pin2
  N1: J1.pin3, R1.Pin_0
  N2: J1.pin4, R2.Pin_0
  N3: J1.pin5, R3.Pin_0
  N4: J1.pin6, R4.Pin_0
  N5: J1.pin7, R5.Pin_0
  N6: J1.pin8, R6.Pin_0
  N7: J1.pin9, R7.Pin_0
  N8: J1.pin10, R8.Pin_0
  N9: J1.pin11, R9.Pin_0
  N10: J1.pin12, R10.Pin_0
  N11: J1.pin13, R11.Pin_0
  N12: J1.pin14, R12.Pin_0
  N13: J1.pin15, R14.Pin_0
  N14: J1.pin16, R13.Pin_0
  N15: J1.pin17, R15.Pin_0
  N16: J1.pin18, R16.Pin_0
  N17: J1.pin19, R17.Pin_0
  N18: J1.pin20, R18.Pin_0
  N19: J1.pin21, R19.Pin_0
  N20: J1.pin22, R20.Pin_0
  N21: J1.pin23, R21.Pin_0
  N22: J1.pin42, S15.Pin_3, S15.Pin_4
  N23: J1.pin43, S16.Pin_3, S16.Pin_4
  N24: J1.pin44, S17.Pin_3, S17.Pin_4
  N25: J1.pin45, S18.Pin_3, S18.Pin_4
  N26: J1.pin46, S19.Pin_3, S19.Pin_4
  N27: J1.pin47, S20.Pin_3, S20.Pin_4
  N28: J1.pin48, S21.Pin_3, S21.Pin_4
  N29: J1.pin49, S8.Pin_3, S8.Pin_4
  N30: J1.pin50, S9.Pin_3, S9.Pin_4
  N31: J1.pin51, S10.Pin_3, S10.Pin_4
  N32: J1.pin52, S11.Pin_3, S11.Pin_4
  N33: J1.pin53, S12.Pin_3, S12.Pin_4
  N34: J1.pin54, S13.Pin_3, S13.Pin_4
  N35: J1.pin55, S14.Pin_3, S14.Pin_4
  N36: J1.pin56, S1.Pin_3, S1.Pin_4
  N37: J1.pin57, S2.Pin_3, S2.Pin_4
  N38: J1.pin58, S3.Pin_3, S3.Pin_4
  N39: J1.pin59, S4.Pin_3, S4.Pin_4
  N40: J1.pin60, S5.Pin_3, S5.Pin_4
  N41: J1.pin61, S6.Pin_3, S6.Pin_4
  N42: J1.pin62, S7.Pin_3, S7.Pin_4
  GND: J1.pin63, J1.pin64, LED1.cathode, S1.Pin_1, S1.Pin_2, S2.Pin_1, S2.Pin_2, S3.Pin_1, S3.Pin_2, S4.Pin_1, S4.Pin_2, S5.Pin_1, S5.Pin_2, S6.Pin_1, S6.Pin_2, S7.Pin_1, S7.Pin_2, LED2.cathode, LED3.cathode, LED4.cathode, LED5.cathode, LED6.cathode, LED7.cathode, LED8.cathode, LED9.cathode, LED10.cathode, LED11.cathode, LED12.cathode, LED13.cathode, LED14.cathode, LED15.cathode, LED16.cathode, LED17.cathode, LED18.cathode, LED19.cathode, LED20.cathode, LED21.cathode, S8.Pin_1, S8.Pin_2, S9.Pin_1, S9.Pin_2, S10.Pin_1, S10.Pin_2, S11.Pin_1, S11.Pin_2, S12.Pin_1, S12.Pin_2, S13.Pin_1, S13.Pin_2, S14.Pin_1, S14.Pin_2, S15.Pin_1, S15.Pin_2, S16.Pin_1, S16.Pin_2, S17.Pin_1, S17.Pin_2, S18.Pin_1, S18.Pin_2, S19.Pin_1, S19.Pin_2, S20.Pin_1, S20.Pin_2, S21.Pin_1, S21.Pin_2
  N43: LED1.anode, R1.Pin_1
  N44: LED2.anode, R2.Pin_1
  N45: LED3.anode, R3.Pin_1
  N46: LED4.anode, R4.Pin_1
  N47: LED5.anode, R5.Pin_1
  N48: LED6.anode, R6.Pin_1
  N49: LED7.anode, R7.Pin_1
  N50: LED8.anode, R8.Pin_1
  N51: LED9.anode, R9.Pin_1
  N52: LED10.anode, R10.Pin_1
  N53: LED11.anode, R11.Pin_1
  N54: LED12.anode, R12.Pin_1
  N55: LED13.anode, R14.Pin_1
  N56: LED14.anode, R13.Pin_1
  N57: LED15.anode, R15.Pin_1
  N58: LED16.anode, R16.Pin_1
  N59: LED17.anode, R17.Pin_1
  N60: LED18.anode, R18.Pin_1
  N61: LED19.anode, R19.Pin_1
  N62: LED20.anode, R20.Pin_1
  N63: LED21.anode, R21.Pin_1

notes:
  All wires and resistors
  are on the under (foil)
  side. Only the connector, LEDs and
  switches are on the top (component) side.

custom parts:
  Generic shrouded header - 64 pins: Generic shrouded header
  Red LED - 5mm: A generic red LED (~1.8V)
  220 Ω Resistor: A generic resistor (0.25W)
